// Logisim project capstone.circ as structural Verilog: 1 circuit, main circuit main
module main (
);

  wire adder_6_cout, and_1_out, CARRY_FLAG, CLK, demultiplexer_1_out1, demultiplexer_1_out2,
       demultiplexer_1_out3, demultiplexer_1_out4, demultiplexer_1_out5, demultiplexer_1_out6,
       demultiplexer_2_out1, demultiplexer_2_out2, demultiplexer_2_out3, demultiplexer_2_out4,
       demultiplexer_2_out5, demultiplexer_2_out6, demultiplexer_2_out7, EDI, OVERFLOW_FLAG, PARITY_FLAG,
       READ_A, READ_FL, READ_I, READ_INS, READ_MEM, READ_P, READ_SP, READ_X, READ_Y, WRITE_A, WRITE_FL,
       WRITE_I, WRITE_INS, WRITE_MEM, WRITE_P, WRITE_X, WRITE_Y, ZERO_FLAG;
  wire [3:0] buffer_6_out, controlled_buffer_1_out_2, controlled_buffer_2_out_2, controlled_buffer_2_out_3,
       controlled_buffer_3_out_2, controlled_buffer_4_out_2, controlled_buffer_5_out_2;
  wire [7:0] adder_1_out, adder_2_out, adder_3_out, adder_4_out, adder_5_out, adder_6_out, and_2_out,
       bit_extender_2_out, controlled_buffer_2_out, INS_Step_Counter_q, multiplexer_1_out, or_1_out,
       Stack_Pointer_q;
  wire [11:0] controlled_buffer_1_out, controlled_buffer_3_out, controlled_buffer_4_out,
       controlled_buffer_5_out;
  wire [15:0] Accumulator_q, bit_extender_1_out, buffer_7_out, DATA_BUS, INS_Lookup_Table_data,
       Instruction_Register_q, Memory_dout, Page_Register_q, Program_Counter_q, X_Register_q, Y_Register_q;
  wire [15:8] buffer_6_out_2;

  // Probe on WRITE_X
  // Probe on WRITE_Y
  // Probe on WRITE_A
  // Probe on WRITE_P
  Clock clock_1 (.out(CLK));
  // Probe on DATA_BUS
  // Probe on READ_X
  // Probe on READ_Y
  // Probe on READ_A
  // Probe on READ_P
  // Probe on WRITE_MEM
  // Probe on READ_MEM
  Register #(.width(16)) X_Register (.D(DATA_BUS), .en(WRITE_X), .clk(CLK), .Q(X_Register_q));  // open: clr
  Register #(.width(16)) Y_Register (.D(DATA_BUS), .en(WRITE_Y), .clk(CLK), .Q(Y_Register_q));  // open: clr
  Register #(.width(16)) Accumulator (.D(DATA_BUS), .en(WRITE_A), .clk(CLK), .Q(Accumulator_q));  // open: clr
  Register #(.width(16)) Page_Register (.D(DATA_BUS), .en(WRITE_P), .clk(CLK), .Q(Page_Register_q));  // open: clr
  Register #(.width(16)) Instruction_Register (
    .D(DATA_BUS), .en(WRITE_INS), .clk(CLK), .Q(Instruction_Register_q));  // open: clr
  Hex_Digit_Display hex_digit_display_1 (.value(controlled_buffer_1_out_2));  // open: dp
  assign {controlled_buffer_1_out_2, controlled_buffer_1_out} = READ_X ? X_Register_q : 16'bz;  // Controlled_Buffer controlled_buffer_1
  assign {controlled_buffer_2_out_3, controlled_buffer_2_out_2, controlled_buffer_2_out} = READ_Y ? Y_Register_q : 16'bz;  // Controlled_Buffer controlled_buffer_2
  assign {controlled_buffer_3_out_2, controlled_buffer_3_out} = READ_A ? Accumulator_q : 16'bz;  // Controlled_Buffer controlled_buffer_3
  assign {controlled_buffer_4_out_2, controlled_buffer_4_out} = READ_P ? Page_Register_q : 16'bz;  // Controlled_Buffer controlled_buffer_4
  assign {controlled_buffer_5_out_2, controlled_buffer_5_out} = READ_INS ? Instruction_Register_q : 16'bz;  // Controlled_Buffer controlled_buffer_5
  // Probe on ZERO_FLAG
  // Probe on CARRY_FLAG
  // Probe on OVERFLOW_FLAG
  // Probe on PARITY_FLAG
  // Probe on READ_INS
  // Probe on READ_SP
  Hex_Digit_Display hex_digit_display_2 (.value(controlled_buffer_1_out[11:8]));  // open: dp
  Hex_Digit_Display hex_digit_display_3 (.value(controlled_buffer_1_out[7:4]));  // open: dp
  assign DATA_BUS = {controlled_buffer_1_out_2, controlled_buffer_1_out};  // Buffer buffer_1, 16 bits wide
  Hex_Digit_Display hex_digit_display_4 (.value(controlled_buffer_2_out_3));  // open: dp
  Hex_Digit_Display hex_digit_display_5 (.value(controlled_buffer_2_out_2));  // open: dp
  Hex_Digit_Display hex_digit_display_6 (.value(controlled_buffer_3_out_2));  // open: dp
  Hex_Digit_Display hex_digit_display_7 (.value(controlled_buffer_3_out[11:8]));  // open: dp
  Hex_Digit_Display hex_digit_display_8 (.value(controlled_buffer_4_out_2));  // open: dp
  Hex_Digit_Display hex_digit_display_9 (.value(controlled_buffer_4_out[11:8]));  // open: dp
  Hex_Digit_Display hex_digit_display_10 (.value(controlled_buffer_5_out_2));  // open: dp
  // Probe on WRITE_INS
  Hex_Digit_Display hex_digit_display_11 (.value(controlled_buffer_1_out[3:0]));  // open: dp
  Hex_Digit_Display hex_digit_display_12 (.value(controlled_buffer_2_out[7:4]));  // open: dp
  assign DATA_BUS = {controlled_buffer_2_out_3, controlled_buffer_2_out_2, controlled_buffer_2_out};  // Buffer buffer_2, 16 bits wide
  Hex_Digit_Display hex_digit_display_13 (.value(controlled_buffer_3_out[7:4]));  // open: dp
  assign DATA_BUS = {controlled_buffer_3_out_2, controlled_buffer_3_out};  // Buffer buffer_3, 16 bits wide
  Hex_Digit_Display hex_digit_display_14 (.value(controlled_buffer_4_out[7:4]));  // open: dp
  assign DATA_BUS = {controlled_buffer_4_out_2, controlled_buffer_4_out};  // Buffer buffer_4, 16 bits wide
  Hex_Digit_Display hex_digit_display_15 (.value(controlled_buffer_5_out[11:8]));  // open: dp
  Hex_Digit_Display hex_digit_display_16 (.value(controlled_buffer_5_out[7:4]));  // open: dp
  assign DATA_BUS = {controlled_buffer_5_out_2, controlled_buffer_5_out};  // Buffer buffer_5, 16 bits wide
  Hex_Digit_Display hex_digit_display_17 (.value(controlled_buffer_2_out[3:0]));  // open: dp
  Hex_Digit_Display hex_digit_display_18 (.value(controlled_buffer_3_out[3:0]));  // open: dp
  Hex_Digit_Display hex_digit_display_19 (.value(controlled_buffer_4_out[3:0]));  // open: dp
  Hex_Digit_Display hex_digit_display_20 (.value(controlled_buffer_5_out[3:0]));  // open: dp
  // Probe on WRITE_FL
  // Probe on READ_FL
  // Probe on EDI
  Counter #(.max('hffff), .width(16)) Program_Counter (
    .clr(1'b0), .load(1'b0), .clk(CLK), .D(DATA_BUS), .Q(Program_Counter_q));  // open: up, count, carry
  Counter Stack_Pointer (
    .clr(1'b0), .load(1'b0), .up(1'b0), .clk(and_1_out), .Q(Stack_Pointer_q));  // open: count, D, carry
  and and_1 (and_1_out, CLK, 1'b0);
  Counter INS_Step_Counter (.clr(EDI), .clk(CLK), .Q(INS_Step_Counter_q));  // open: load, up, count, D, carry
  assign {buffer_6_out_2, buffer_6_out, PARITY_FLAG, OVERFLOW_FLAG, CARRY_FLAG, ZERO_FLAG} = DATA_BUS;  // Buffer buffer_6, 16 bits wide
  Adder adder_1 (.a(Stack_Pointer_q), .b({8{1'b1}}), .out(adder_1_out));  // open: cin, cout
  Adder adder_2 (.a(buffer_6_out_2), .b(INS_Step_Counter_q), .out(adder_2_out));  // open: cin, cout
  RAM #(.addrWidth(16), .dataWidth(16)) Memory (
    .addr(Program_Counter_q), .we(WRITE_MEM), .oe(READ_MEM), .clk(CLK), .din(buffer_7_out), .dout(Memory_dout));
  assign buffer_7_out = DATA_BUS;  // Buffer buffer_7, 16 bits wide
  assign bit_extender_1_out = {{8{1'b0}}, adder_1_out};  // Bit_Extender bit_extender_1
  assign bit_extender_2_out = {{4{1'b0}}, buffer_6_out};  // Bit_Extender bit_extender_2
  // Probe on INS_Step_Counter_q
  // Probe on adder_2_out
  // Probe on adder_2_out
  ROM #(.dataWidth(16)) INS_Lookup_Table (
    .addr(adder_2_out), .data({INS_Lookup_Table_data[15:6], EDI, INS_Lookup_Table_data[4:0]}));
  assign DATA_BUS = READ_SP ? bit_extender_1_out : 16'bz;  // Controlled_Buffer controlled_buffer_6
  ROM #(.dataWidth(16)) AM_Lookup_Table (.addr(adder_3_out));  // open: data
  Adder adder_3 (.a(bit_extender_2_out), .b(INS_Step_Counter_q), .out(adder_3_out));  // open: cin, cout
  // Probe on INS_Lookup_Table_data[12:10]
  // Probe on INS_Lookup_Table_data[15:13]
  Demultiplexer #(.select(3)) demultiplexer_1 (
    .out1(demultiplexer_1_out1), .out2(demultiplexer_1_out2), .out3(demultiplexer_1_out3),
    .out4(demultiplexer_1_out4), .out5(demultiplexer_1_out5), .out6(demultiplexer_1_out6), .in(1'b1),
    .sel(INS_Lookup_Table_data[15:13]));  // open: out0, out7
  // Probe on Memory_dout
  assign DATA_BUS = Memory_dout;  // Buffer buffer_8, 16 bits wide
  Demultiplexer #(.select(3)) demultiplexer_2 (
    .out1(demultiplexer_2_out1), .out2(demultiplexer_2_out2), .out3(demultiplexer_2_out3),
    .out4(demultiplexer_2_out4), .out5(demultiplexer_2_out5), .out6(demultiplexer_2_out6),
    .out7(demultiplexer_2_out7), .in(1'b1), .sel(INS_Lookup_Table_data[12:10]));  // open: out0
  buf buffer_9 (WRITE_X, demultiplexer_1_out1);
  buf buffer_10 (WRITE_Y, demultiplexer_1_out2);
  buf buffer_11 (WRITE_A, demultiplexer_1_out3);
  buf buffer_12 (WRITE_P, demultiplexer_1_out4);
  buf buffer_13 (WRITE_I, demultiplexer_1_out5);
  buf buffer_14 (WRITE_MEM, demultiplexer_1_out6);
  buf buffer_15 (READ_X, demultiplexer_2_out1);
  buf buffer_16 (READ_Y, demultiplexer_2_out2);
  buf buffer_17 (READ_A, demultiplexer_2_out3);
  buf buffer_18 (READ_P, demultiplexer_2_out4);
  buf buffer_19 (READ_I, demultiplexer_2_out5);
  buf buffer_20 (READ_MEM, demultiplexer_2_out6);
  buf buffer_21 (READ_SP, demultiplexer_2_out7);
  Adder adder_4 (.a(8'h2), .b(8'h1), .out(adder_4_out));  // open: cin, cout
  Adder adder_5 (.a({8{1'b1}}), .b(8'h1), .out(adder_5_out));  // open: cin, cout
  Adder adder_6 (.a(8'h2), .b({8{1'b1}}), .out(adder_6_out), .cout(adder_6_cout));  // open: cin
  // Probe on adder_6_cout
  assign and_2_out = 8'h2 & {8{1'b1}};  // AND_Gate and_2, 8 bits wide
  assign or_1_out = 8'h2 | {8{1'b1}};  // OR_Gate or_1, 8 bits wide
  Multiplexer #(.select(4), .width(8)) multiplexer_1 (
    .in0(adder_4_out), .in1(adder_5_out), .in2(adder_6_out), .in3(and_2_out), .in4(or_1_out),
    .out(multiplexer_1_out), .sel(4'b0010));  // open: in5, in6, in7, in8, in9, in10, in11, in12, in13, in14, in15
  // Probe on multiplexer_1_out

  // Notes on the sheet:
  //   Flags
  //   Load PC Value
  //   contents of INS_Lookup_Table (hex, n*v repeats v):
  //   20 7800 7800 20
  //   Instruction Decoder
  //   ALU
endmodule
